// Logisim project bladeprod.circ as structural Verilog: 3 circuits, main circuit blademult
module blademult (
  input  [4:0] blade_1,
  input  [4:0] blade_2,
  input  [31:0] in_3,
  input  [31:0] in_4
);


  // Notes on the sheet:
  //   coefficient 1
  //   coefficient 2
endmodule

module _5_to_32_Decoder (
  input  s4,
  input  s3,
  input  s2,
  input  s1,
  input  s0,
  output [31:0] out_6
);

  wire not_1_out, not_2_out, not_3_out, not_4_out, not_5_out, undriven, undriven_2, undriven_3, undriven_4,
       undriven_5, undriven_6, undriven_7, undriven_8, undriven_9, undriven_10, undriven_11, undriven_12,
       undriven_13, undriven_14, undriven_15, undriven_16, undriven_17, undriven_18, undriven_19,
       undriven_20, undriven_21, undriven_22, undriven_23, undriven_24, undriven_25, undriven_26,
       undriven_27, undriven_28, undriven_29, undriven_30;

  not not_1 (not_1_out, s4);
  not not_2 (not_2_out, s2);
  not not_3 (not_3_out, s3);
  not not_4 (not_4_out, s1);
  not not_5 (not_5_out, s0);
  and and_1 (out_6[0], not_1_out, not_3_out, not_2_out, not_4_out, not_5_out);
  and and_2 (out_6[1], s0, not_4_out, not_2_out, not_3_out, not_1_out);
  and and_3 (out_6[2], undriven, undriven_2, undriven_3, undriven_4, undriven_5);
  and and_4 (out_6[3], undriven_6, undriven_7, undriven_8, undriven_9, undriven_10);
  and and_5 (out_6[4], undriven_11, undriven_12, undriven_13, undriven_14, undriven_15);
  and and_6 (out_6[5], undriven_16, undriven_17, undriven_18, undriven_19, undriven_20);
  and and_7 (out_6[6], undriven_21, undriven_22, undriven_23, undriven_24, undriven_25);
  and and_8 (out_6[7], undriven_26, undriven_27, undriven_28, undriven_29, undriven_30);
  // AND_Gate and_9 has open pins: out=out_6[8]
  // AND_Gate and_10 has open pins: out=out_6[9]
  // AND_Gate and_11 has open pins: out=out_6[10]
  // AND_Gate and_12 has open pins: out=out_6[11]
  // AND_Gate and_13 has open pins: out=out_6[12]
  // AND_Gate and_14 has open pins: out=out_6[13]
  // AND_Gate and_15 has open pins: out=out_6[14]
  // AND_Gate and_16 has open pins: out=out_6[15]
  // AND_Gate and_17 has open pins: out=out_6[16]
  // AND_Gate and_18 has open pins: out=out_6[17]
  // AND_Gate and_19 has open pins: out=out_6[18]
  // AND_Gate and_20 has open pins: out=out_6[19]
  // AND_Gate and_21 is placed but not wired
  // AND_Gate and_22 is placed but not wired
  // AND_Gate and_23 is placed but not wired
  // AND_Gate and_24 is placed but not wired
  // AND_Gate and_25 is placed but not wired
  // AND_Gate and_26 is placed but not wired
  // AND_Gate and_27 is placed but not wired
  // AND_Gate and_28 is placed but not wired
  // AND_Gate and_29 is placed but not wired
  // AND_Gate and_30 has open pins: in0=s4, in1=not_3_out, in2=s2, in4=s0, out=open
  // AND_Gate and_31 has open pins: in0=not_1_out, in1=s3, in2=s2, in3=s1, in4=s0, out=open
  // AND_Gate and_32 has open pins: in0=s4, in1=s3, in2=s2, in3=s1, in4=s0, out=open

  // Notes on the sheet:
  //   Least Significant Bit
  //   Output
endmodule

module conditionalIncrement (
  input  Enable,
  input  [31:0] in_2
);


  // Notes on the sheet:
  //   32 bit coefficient
endmodule
